# Fritzing sketch lime.v03 (saved by Fritzing 0.9.6b)
perfboards: 1

parts:
  WeMos_D1_Mini1 = WeMos D1 Mini
  R5 = Resistor [tolerance=±5% power=0.25 resistance=3.75M package=THT]
  R3 = Resistor [tolerance=±5% power=0.25 resistance=10k package=THT]
  Q1-3906 = NPN-Transistor [package="TO92 [THT]"]

nets:
  N1: WeMos_D1_Mini1.3V3, R3.Pin_1
  N2: WeMos_D1_Mini1.A0, R5.Pin_1
  N3: WeMos_D1_Mini1.G, Q1-3906.C
  N4: WeMos_D1_Mini1.RX, R3.Pin_0, Q1-3906.E
